# Fritzing sketch BleSdRemote (saved by Fritzing 0.9.3b)
breadboards: 1

parts:
  Part1 = Adafruit Bluefruit LE UART Friend [part_number="Adafruit #2479"]
  Part2 = Arduino Mega 2560 (Rev3)
  Part3 = MicroSD Card Module
  VCC1 = Battery block 9V

nets:
  GND: Part1.GND, Part1.CTS, Part2.GND, Part3.GND, VCC1.-
  VIN: Part1.VIN, Part2.5V
  N1: Part1.RXI, Part2.D18/TX1
  N2: Part1.TXO, Part2.D19/RX1
  3V3: Part2.3V3, Part3.VCC
  N3: Part2.VIN, VCC1.+
  N4: Part2.D50, Part3.MISO
  N5: Part2.D51, Part3.MOSI
  N6: Part2.D52, Part3.SCK
  N7: Part2.D53, Part3.CS

custom parts:
  Adafruit Bluefruit LE UART Friend: The Bluefruit LE UART Friend makes it easy to add Bluetooth Low Energy connectivity to anything with a hardware or software serial port. We even have nice hardware flow control so you won't have to think about losing data. Connect to your Arduino or other microcontroller or even just a standard FTDI cable for debugging and testing.
